# Fritzing sketch DetermindRemote (saved by Fritzing 0.9.3b)

parts:
  Part1 = Arduino Uno (Rev3)
  Part2 = Thumb Joystick
  Part3 = NRF24L01+ Breakout Board
  BAT1 = BC9VPC [package=bc9vpc]
  S1 = Taiway 100-SP-X-T1 SPDT Miniature Toggle Switch [part_number=100-SP-X-T1-0-0-B1-M2 package=THT]

nets:
  N1: Part1.A0, Part2.HORZ
  N2: Part1.A1, Part2.VERT
  N3: Part1.D9_PWM, Part3.CE
  N4: Part1.D10_PWM/SS, Part3.CS
  N5: Part1.D11_PWM/MOSI, Part3.MOSI
  N6: Part1.D12/MISO, Part3.MISO
  N7: Part1.D13/SCK, Part3.SCK
  GND: Part1.GND, Part2.GND, Part3.GND, BAT1.V-
  3V3: Part1.3V3, Part3.VCC
  5V: Part1.5V, Part2.VCC
  N8: Part1.VIN, S1.L1
  N9: BAT1.V+, S1.COM
