# Fritzing sketch DetermindRobot (saved by Fritzing 0.9.3b)

parts:
  Part1 = Arduino Uno (Rev3)
  Part2 = NRF24L01+ Breakout Board
  S2 = Taiway 100-SP-X-T1 SPDT Miniature Toggle Switch [part_number=100-SP-X-T1-0-0-B1-M1 package=THT]
  S3 = Taiway 100-SP-X-T1 SPDT Miniature Toggle Switch [part_number=100-SP-X-T1-0-0-B1-M1 package=THT]
  BAT1 = BC9VPC [package=bc9vpc]
  M1 = DC Motor
  M2 = DC Motor
  VCC1 = 4 x AAA Battery Mount
  S4 = H-Bridge with L298N

nets:
  N1: Part1.D8, Part2.CE
  N2: Part1.D9_PWM, S4.IN4
  N3: Part1.D10_PWM/SS, Part2.CS
  N4: Part1.D11_PWM/MOSI, Part2.MOSI
  N5: Part1.D12/MISO, Part2.MISO
  N6: Part1.D13/SCK, Part2.SCK
  GND: Part1.GND, Part2.GND, BAT1.V-, VCC1.-, S4.GND
  N7: Part1.D3_PWM, S4.IN1
  N8: Part1.D5_PWM, S4.IN2
  N9: Part1.D6_PWM, S4.IN3
  3V3: Part1.3V3, Part2.VCC
  N10: Part1.VIN, S3.COM
  N11: S2.COM, S4.12V
  N12: S2.L1, VCC1.+
  N13: S3.L1, BAT1.V+
  N14: M1.pin_1, S4.M1-02
  N15: M1.pin_2, S4.M1-01
  N16: M2.pin_1, S4.M2-02
  N17: M2.pin_2, S4.M2-01
  N18: S4.ENA, S4.ENA-5V
  N19: S4.ENB, S4.ENB-5V

custom parts:
  H-Bridge with L298N: h-bridge
